# Fritzing sketch cilite (saved by Fritzing 0.7.12b)
breadboards: 1

parts:
  LED1 = RGB LED - (4 legs) [package="5 mm [THT]"]
  RGB_Shield = Arduino
  R5 = 330 Ω Resistor [package=THT]
  R6 = 330 Ω Resistor [package=THT]
  R7 = 330 Ω Resistor [package=THT]

nets:
  N1: LED1.red_cathode, R5.Pin_0
  N2: LED1.green_cathode, R7.Pin_0
  N3: LED1.blue_cathode, R6.Pin_0
  N4: RGB_Shield.D11, R5.Pin_1
  N5: RGB_Shield.D10, R7.Pin_1
  N6: RGB_Shield.D9, R6.Pin_1
